# Fritzing sketch control-allmotors (saved by Fritzing 0.9.10b)
circuit board: 8.46667cm x 5.64444cm

parts:
  M4 = DC Motor [voltage_(max)=6V voltage_(min)=3V]
  S1 = H-Bridge with L298N
  Part1 = Arduino Uno (Rev3)
  M6 = DC Motor [voltage_(max)=6V voltage_(min)=3V]
  Part2 = HC-05 [part_number=HC-05 package="breakout board"]
  BAT1 = BC9VPC [package=bc9vpc]
  M1 = DC Motor [voltage_(max)=6V voltage_(min)=3V]
  M5 = DC Motor [voltage_(max)=6V voltage_(min)=3V]
  J1 = Basic Servo
  U1 = Voltage Regulator - 5V [package="TO220 [THT]"]
  BAT2 = BC9VPC [package=bc9vpc]
  M7 = Stepper Motor - Bipolar
  Pololu_A1 = Pololu A4988 [package=SO16]

nets (from the breadboard view):
  N1: M4.pin_1, S1.M1-01, M6.pin_1
  N2: M4.pin_2, S1.M1-02, M6.pin_2
  N3: S1.12V, BAT1.V+, U1.input_voltage
  GND: S1.GND, Part1.GND, Part2.GND, BAT1.V-, J1.gnd, U1.GND, Pololu_A1.GND#8
  N4: S1.ENA, S1.ENB, Part1.D11_PWM/MOSI
  N5: S1.IN1, Part1.D5_PWM
  N6: S1.IN2, Part1.D4
  N7: S1.IN3, Part1.D3_PWM
  N8: S1.IN4, Part1.D2
  N9: S1.M2-01, M1.pin_2, M5.pin_2
  N10: S1.M2-02, M1.pin_1, M5.pin_1
  N11: Part1.D9_PWM, J1.pulse
  N12: Part1.D10_PWM/SS, Pololu_A1.ENABLE
  N13: Part1.D12/MISO, Pololu_A1.STEP
  N14: Part1.D13/SCK, Pololu_A1.DIR
  N15: Part1.D0/RX, Part2.TXD
  N16: Part1.D1/TX, Part2.RXD
  5V: Part1.5V, Part2.VCC, Pololu_A1.VDD
  N17: J1.vcc, U1.output_voltage
  N18: BAT2.V+, Pololu_A1.VMOT
  N19: BAT2.V-, Pololu_A1.GND#14
  N20: M7.A, Pololu_A1.2B
  N21: M7.C, Pololu_A1.2A
  N22: M7.B, Pololu_A1.1A
  N23: M7.D, Pololu_A1.1B
  N24: Pololu_A1.RESET, Pololu_A1.SLEEP

custom parts:
  H-Bridge with L298N: h-bridge
  HC-05: A commonly available HC-05 Bluetooth breakout board.
